# Fritzing sketch weather_station (saved by Fritzing 0.9.2b)
breadboards: 1

parts:
  part = Arduino Uno (Rev3)
  part_2 = Resistor [tolerance=±5% resistance=10k package="1206 [SMD]"]
  Antenna_17_cm_wire = Antenna
  Switch = Momentary Switch [package=ksa_sealed_tac_switch]
  433_MHz_transmiter = RF-LINK_TX [package=rf-link_tx]

nets:
  GND: part.GND, part_2.Pin_1, 433_MHz_transmiter.GND
  N1: part.D2, part_2.Pin_0, Switch.2
  N2: part.D3_PWM, 433_MHz_transmiter.DATA
  5V: part.5V, Switch.4, 433_MHz_transmiter.+5V
  N3: Antenna_17_cm_wire.antenna_lead, 433_MHz_transmiter.ANT
